// Logisim project alu.circ as structural Verilog: 10 circuits, main circuit alu
module alu (
  input  [31:0] A,
  input  [31:0] B,
  input  [3:0] ALUSel,
  input  in_4,
  input  in_5,
  output [31:0] Result
);

  wire [31:0] R1, R2, R3, R4, R5, R6, R7, R8, R9, undriven;

  assign R2 = A & B;  // AND_Gate and_1, 32 bits wide
  assign R3 = A | B;  // OR_Gate or_1, 32 bits wide
  assign R4 = A ^ B;  // XOR_Gate xor_1, 32 bits wide
  assign R5 = ~A;  // NOT_Gate not_1, 32 bits wide
  overallSRA overallsra_1 (.A(A), .in_2(B), .sraOutput(R6));
  overallAdd overalladd_1 (.A(A), .B(B), .addOut(R1));
  overallSLL overallsll_1 (.A(A), .B(B), .shiftOut(R7));
  overallSLT overallslt_1 (.A(A), .B(B), .SLTout(R8));
  overallSubtract overallsubtract_1 (.A(A), .B(B), .subtractOut(R9));
  Multiplexer #(.select(4), .width(32), .enable("false")) multiplexer_1 (
    .in0(R1), .in1(R2), .in2(R3), .in3(R4), .in4(R5), .in5(R6), .in6(R7), .in7(R8), .in8(R9), .in9(undriven),
    .in10(undriven), .in11(undriven), .in12(undriven), .in13(undriven), .in14(undriven), .in15(undriven),
    .out(Result), .sel(ALUSel));

  assign in_5 = in_4;

  // Notes on the sheet:
  //   INPUTS to your circuit
  //   DON'T CHANGE THE LOCATIONS OF THE INPUTS AND OUTPUTS!
  //   OUTPUT from your circuit
endmodule

module adderCirc (
  input  addA,
  input  addB,
  input  addC,
  output sumOut,
  output COut
);

  wire and_1_out, and_2_out, and_3_out, and_4_out, and_5_out, and_6_out, and_7_out, not_1_out, not_2_out,
       not_3_out;

  not not_1 (not_1_out, addA);
  not not_2 (not_2_out, addB);
  not not_3 (not_3_out, addC);
  and and_1 (and_1_out, not_1_out, not_2_out, addC);
  and and_2 (and_2_out, not_1_out, addB, not_3_out);
  and and_3 (and_3_out, addA, not_2_out, not_3_out);
  and and_4 (and_4_out, addA, addB, addC);
  and and_5 (and_5_out, not_1_out, addB, addC);
  and and_6 (and_6_out, addA, not_2_out, addC);
  and and_7 (and_7_out, addA, addB, not_3_out);
  or or_1 (sumOut, and_1_out, and_2_out, and_3_out, and_4_out);
  or or_2 (COut, and_4_out, and_5_out, and_6_out, and_7_out);
endmodule

module overallAdd (
  input  [31:0] A,
  input  [31:0] B,
  output [31:0] addOut
);

  wire addercirc_1_cout, addercirc_2_cout, addercirc_3_cout, addercirc_4_cout, addercirc_5_cout,
       addercirc_6_cout, addercirc_7_cout, addercirc_8_cout, addercirc_9_cout, addercirc_10_cout,
       addercirc_11_cout, addercirc_12_cout, addercirc_13_cout, addercirc_14_cout, addercirc_15_cout,
       addercirc_16_cout, addercirc_17_cout, addercirc_18_cout, addercirc_19_cout, addercirc_20_cout,
       addercirc_21_cout, addercirc_22_cout, addercirc_23_cout, addercirc_24_cout, addercirc_25_cout,
       addercirc_26_cout, addercirc_27_cout, addercirc_28_cout, addercirc_29_cout, addercirc_30_cout,
       addercirc_31_cout;

  adderCirc addercirc_1 (.addA(A[0]), .addB(B[0]), .addC(1'b0), .sumOut(addOut[0]), .COut(addercirc_1_cout));
  adderCirc addercirc_2 (
    .addA(A[1]), .addB(B[1]), .addC(addercirc_1_cout), .sumOut(addOut[1]), .COut(addercirc_2_cout));
  adderCirc addercirc_3 (
    .addA(A[2]), .addB(B[2]), .addC(addercirc_2_cout), .sumOut(addOut[2]), .COut(addercirc_3_cout));
  adderCirc addercirc_4 (
    .addA(A[3]), .addB(B[3]), .addC(addercirc_3_cout), .sumOut(addOut[3]), .COut(addercirc_4_cout));
  adderCirc addercirc_5 (
    .addA(A[4]), .addB(B[4]), .addC(addercirc_4_cout), .sumOut(addOut[4]), .COut(addercirc_5_cout));
  adderCirc addercirc_6 (
    .addA(A[5]), .addB(B[5]), .addC(addercirc_5_cout), .sumOut(addOut[5]), .COut(addercirc_6_cout));
  adderCirc addercirc_7 (
    .addA(A[6]), .addB(B[6]), .addC(addercirc_6_cout), .sumOut(addOut[6]), .COut(addercirc_7_cout));
  adderCirc addercirc_8 (
    .addA(A[7]), .addB(B[7]), .addC(addercirc_7_cout), .sumOut(addOut[7]), .COut(addercirc_8_cout));
  adderCirc addercirc_9 (
    .addA(A[8]), .addB(B[8]), .addC(addercirc_8_cout), .sumOut(addOut[8]), .COut(addercirc_9_cout));
  adderCirc addercirc_10 (
    .addA(A[9]), .addB(B[9]), .addC(addercirc_9_cout), .sumOut(addOut[9]), .COut(addercirc_10_cout));
  adderCirc addercirc_11 (
    .addA(A[10]), .addB(B[10]), .addC(addercirc_10_cout), .sumOut(addOut[10]), .COut(addercirc_11_cout));
  adderCirc addercirc_12 (
    .addA(A[11]), .addB(B[11]), .addC(addercirc_11_cout), .sumOut(addOut[11]), .COut(addercirc_12_cout));
  adderCirc addercirc_13 (
    .addA(A[12]), .addB(B[12]), .addC(addercirc_12_cout), .sumOut(addOut[12]), .COut(addercirc_13_cout));
  adderCirc addercirc_14 (
    .addA(A[13]), .addB(B[13]), .addC(addercirc_13_cout), .sumOut(addOut[13]), .COut(addercirc_14_cout));
  adderCirc addercirc_15 (
    .addA(A[14]), .addB(B[14]), .addC(addercirc_14_cout), .sumOut(addOut[14]), .COut(addercirc_15_cout));
  adderCirc addercirc_16 (
    .addA(A[15]), .addB(B[15]), .addC(addercirc_15_cout), .sumOut(addOut[15]), .COut(addercirc_16_cout));
  adderCirc addercirc_17 (
    .addA(A[16]), .addB(B[16]), .addC(addercirc_16_cout), .sumOut(addOut[16]), .COut(addercirc_17_cout));
  adderCirc addercirc_18 (
    .addA(A[17]), .addB(B[17]), .addC(addercirc_17_cout), .sumOut(addOut[17]), .COut(addercirc_18_cout));
  adderCirc addercirc_19 (
    .addA(A[18]), .addB(B[18]), .addC(addercirc_18_cout), .sumOut(addOut[18]), .COut(addercirc_19_cout));
  adderCirc addercirc_20 (
    .addA(A[19]), .addB(B[19]), .addC(addercirc_19_cout), .sumOut(addOut[19]), .COut(addercirc_20_cout));
  adderCirc addercirc_21 (
    .addA(A[20]), .addB(B[20]), .addC(addercirc_20_cout), .sumOut(addOut[20]), .COut(addercirc_21_cout));
  adderCirc addercirc_22 (
    .addA(A[21]), .addB(B[21]), .addC(addercirc_21_cout), .sumOut(addOut[21]), .COut(addercirc_22_cout));
  adderCirc addercirc_23 (
    .addA(A[22]), .addB(B[22]), .addC(addercirc_22_cout), .sumOut(addOut[22]), .COut(addercirc_23_cout));
  adderCirc addercirc_24 (
    .addA(A[23]), .addB(B[23]), .addC(addercirc_23_cout), .sumOut(addOut[23]), .COut(addercirc_24_cout));
  adderCirc addercirc_25 (
    .addA(A[24]), .addB(B[24]), .addC(addercirc_24_cout), .sumOut(addOut[24]), .COut(addercirc_25_cout));
  adderCirc addercirc_26 (
    .addA(A[25]), .addB(B[25]), .addC(addercirc_25_cout), .sumOut(addOut[25]), .COut(addercirc_26_cout));
  adderCirc addercirc_27 (
    .addA(A[26]), .addB(B[26]), .addC(addercirc_26_cout), .sumOut(addOut[26]), .COut(addercirc_27_cout));
  adderCirc addercirc_28 (
    .addA(A[27]), .addB(B[27]), .addC(addercirc_27_cout), .sumOut(addOut[27]), .COut(addercirc_28_cout));
  adderCirc addercirc_29 (
    .addA(A[28]), .addB(B[28]), .addC(addercirc_28_cout), .sumOut(addOut[28]), .COut(addercirc_29_cout));
  adderCirc addercirc_30 (
    .addA(A[29]), .addB(B[29]), .addC(addercirc_29_cout), .sumOut(addOut[29]), .COut(addercirc_30_cout));
  adderCirc addercirc_31 (
    .addA(A[30]), .addB(B[30]), .addC(addercirc_30_cout), .sumOut(addOut[30]), .COut(addercirc_31_cout));
  adderCirc addercirc_32 (.addA(A[31]), .addB(B[31]), .addC(addercirc_31_cout), .sumOut(addOut[31]));  // open: COut

  // Other names for the same wires on the sheet: AA0 = A[0]; AA1 = A[1]; AA2 = A[2]; AA3 = A[3]; AA4 = A[4];
  //   AA5 = A[5]; AA6 = A[6]; AA7 = A[7]; AA8 = A[8]; AA9 = A[9]; AA10 = A[10]; AA11 = A[11]; AA12 = A[12];
  //   AA13 = A[13]; AA14 = A[14]; AA15 = A[15]; AA16 = A[16]; AA17 = A[17]; AA18 = A[18]; AA19 = A[19]; AA20 = A[20];
  //   AA21 = A[21]; AA22 = A[22]; AA23 = A[23]; AA24 = A[24]; AA25 = A[25]; AA26 = A[26]; AA27 = A[27]; AA28 = A[28];
  //   AA29 = A[29]; AA30 = A[30]; AA31 = A[31]; BA0 = B[0]; BA1 = B[1]; BA2 = B[2]; BA3 = B[3]; BA4 = B[4];
  //   BA5 = B[5]; BA6 = B[6]; BA7 = B[7]; BA8 = B[8]; BA9 = B[9]; BA10 = B[10]; BA11 = B[11]; BA12 = B[12];
  //   BA13 = B[13]; BA14 = B[14]; BA15 = B[15]; BA16 = B[16]; BA17 = B[17]; BA18 = B[18]; BA19 = B[19]; BA20 = B[20];
  //   BA21 = B[21]; BA22 = B[22]; BA23 = B[23]; BA24 = B[24]; BA25 = B[25]; BA26 = B[26]; BA27 = B[27]; BA28 = B[28];
  //   BA29 = B[29]; BA30 = B[30]; BA31 = B[31]
endmodule

module overallSRA (
  input  [31:0] A,
  input  [31:0] in_2,
  output [31:0] sraOutput
);

  wire multiplexer_2_out, multiplexer_3_out, multiplexer_4_out, multiplexer_5_out, multiplexer_6_out,
       multiplexer_7_out, multiplexer_8_out, multiplexer_9_out, multiplexer_10_out, multiplexer_11_out,
       multiplexer_12_out, multiplexer_13_out, multiplexer_14_out, multiplexer_15_out, multiplexer_16_out,
       multiplexer_17_out, multiplexer_18_out, multiplexer_19_out, multiplexer_20_out, multiplexer_21_out,
       multiplexer_22_out, multiplexer_23_out, multiplexer_24_out, multiplexer_25_out, multiplexer_26_out,
       multiplexer_27_out, multiplexer_28_out, multiplexer_29_out, multiplexer_30_out, multiplexer_31_out,
       multiplexer_32_out, multiplexer_33_out, multiplexer_34_out, multiplexer_35_out, multiplexer_36_out,
       multiplexer_37_out, multiplexer_38_out, multiplexer_39_out, multiplexer_40_out, multiplexer_41_out,
       multiplexer_42_out, multiplexer_43_out, multiplexer_44_out, multiplexer_45_out, multiplexer_46_out,
       multiplexer_47_out, multiplexer_48_out, multiplexer_49_out, multiplexer_50_out, multiplexer_51_out,
       multiplexer_52_out, multiplexer_53_out, multiplexer_54_out, multiplexer_55_out, multiplexer_56_out,
       multiplexer_57_out, multiplexer_58_out, multiplexer_59_out, multiplexer_60_out, multiplexer_61_out,
       multiplexer_62_out, multiplexer_63_out, multiplexer_64_out, multiplexer_65_out, multiplexer_66_out,
       multiplexer_67_out, multiplexer_68_out, multiplexer_69_out, multiplexer_70_out, multiplexer_71_out,
       multiplexer_72_out, multiplexer_73_out, multiplexer_74_out, multiplexer_75_out, multiplexer_76_out,
       multiplexer_77_out, multiplexer_78_out, multiplexer_79_out, multiplexer_80_out, multiplexer_81_out,
       multiplexer_82_out, multiplexer_83_out, multiplexer_84_out, multiplexer_85_out, multiplexer_86_out,
       multiplexer_87_out, multiplexer_88_out, multiplexer_89_out, multiplexer_90_out, multiplexer_91_out,
       multiplexer_92_out, multiplexer_93_out, multiplexer_94_out, multiplexer_95_out, multiplexer_96_out,
       multiplexer_97_out, multiplexer_98_out, multiplexer_99_out, multiplexer_100_out, multiplexer_101_out,
       multiplexer_102_out, multiplexer_103_out, multiplexer_104_out, multiplexer_105_out,
       multiplexer_106_out, multiplexer_107_out, multiplexer_108_out, multiplexer_109_out,
       multiplexer_110_out, multiplexer_111_out, multiplexer_112_out, multiplexer_113_out,
       multiplexer_114_out, multiplexer_115_out, multiplexer_116_out, multiplexer_117_out,
       multiplexer_118_out, multiplexer_119_out, multiplexer_120_out, multiplexer_121_out,
       multiplexer_122_out, multiplexer_123_out, multiplexer_124_out, multiplexer_125_out,
       multiplexer_126_out, multiplexer_127_out, multiplexer_128_out, multiplexer_129_out, O1, O2, O3, O4,
       O5, O6, O7, O8, O9, O10, O11, O12, O13, O14, O15, O16, O17, O18, O19, O20, O21, O22, O23, O24, O25,
       O26, O27, O28, O29, O30, O31, O32, or_1_out;

  or or_1 (or_1_out, in_2[5], in_2[6], in_2[7], in_2[8], in_2[9], in_2[10], in_2[11], in_2[12], in_2[13], in_2[14], in_2[15], in_2[16], in_2[17], in_2[18], in_2[19], in_2[20], in_2[21], in_2[22], in_2[23], in_2[24], in_2[25], in_2[26], in_2[27], in_2[28], in_2[29], in_2[30], in_2[31]);
  Multiplexer #(.width(32), .enable("false")) multiplexer_1 (
    .in0({O1, O2, O3, O4, O5, O6, O7, O8, O9, O10, O11, O12, O13, O14, O15, O16, O17, O18, O19, O20, O21, O22, O23, O24, O25, O26, O27, O28, O29, O30, O31, O32}),
    .in1({32{1'b0}}), .out(sraOutput), .sel(or_1_out));
  Multiplexer #(.enable("false")) multiplexer_2 (.in0(A[31]), .in1(A[31]), .out(multiplexer_2_out), .sel(in_2[0]));
  Multiplexer #(.enable("false")) multiplexer_3 (.in0(A[30]), .in1(A[31]), .out(multiplexer_3_out), .sel(in_2[0]));
  Multiplexer #(.enable("false")) multiplexer_4 (.in0(A[29]), .in1(A[30]), .out(multiplexer_4_out), .sel(in_2[0]));
  Multiplexer #(.enable("false")) multiplexer_5 (.in0(A[28]), .in1(A[29]), .out(multiplexer_5_out), .sel(in_2[0]));
  Multiplexer #(.enable("false")) multiplexer_6 (.in0(A[27]), .in1(A[28]), .out(multiplexer_6_out), .sel(in_2[0]));
  Multiplexer #(.enable("false")) multiplexer_7 (.in0(A[26]), .in1(A[27]), .out(multiplexer_7_out), .sel(in_2[0]));
  Multiplexer #(.enable("false")) multiplexer_8 (.in0(A[25]), .in1(A[26]), .out(multiplexer_8_out), .sel(in_2[0]));
  Multiplexer #(.enable("false")) multiplexer_9 (.in0(A[24]), .in1(A[26]), .out(multiplexer_9_out), .sel(in_2[0]));
  Multiplexer #(.enable("false")) multiplexer_10 (.in0(A[23]), .in1(A[24]), .out(multiplexer_10_out), .sel(in_2[0]));
  Multiplexer #(.enable("false")) multiplexer_11 (.in0(A[22]), .in1(A[23]), .out(multiplexer_11_out), .sel(in_2[0]));
  Multiplexer #(.enable("false")) multiplexer_12 (.in0(A[21]), .in1(A[22]), .out(multiplexer_12_out), .sel(in_2[0]));
  Multiplexer #(.enable("false")) multiplexer_13 (.in0(A[20]), .in1(A[21]), .out(multiplexer_13_out), .sel(in_2[0]));
  Multiplexer #(.enable("false")) multiplexer_14 (.in0(A[19]), .in1(A[20]), .out(multiplexer_14_out), .sel(in_2[0]));
  Multiplexer #(.enable("false")) multiplexer_15 (.in0(A[18]), .in1(A[19]), .out(multiplexer_15_out), .sel(in_2[0]));
  Multiplexer #(.enable("false")) multiplexer_16 (.in0(A[17]), .in1(A[18]), .out(multiplexer_16_out), .sel(in_2[0]));
  Multiplexer #(.enable("false")) multiplexer_17 (.in0(A[16]), .in1(A[17]), .out(multiplexer_17_out), .sel(in_2[0]));
  Multiplexer #(.enable("false")) multiplexer_18 (.in0(A[15]), .in1(A[16]), .out(multiplexer_18_out), .sel(in_2[0]));
  Multiplexer #(.enable("false")) multiplexer_19 (.in0(A[14]), .in1(A[15]), .out(multiplexer_19_out), .sel(in_2[0]));
  Multiplexer #(.enable("false")) multiplexer_20 (.in0(A[13]), .in1(A[14]), .out(multiplexer_20_out), .sel(in_2[0]));
  Multiplexer #(.enable("false")) multiplexer_21 (.in0(A[12]), .in1(A[13]), .out(multiplexer_21_out), .sel(in_2[0]));
  Multiplexer #(.enable("false")) multiplexer_22 (.in0(A[11]), .in1(A[12]), .out(multiplexer_22_out), .sel(in_2[0]));
  Multiplexer #(.enable("false")) multiplexer_23 (.in0(A[10]), .in1(A[11]), .out(multiplexer_23_out), .sel(in_2[0]));
  Multiplexer #(.enable("false")) multiplexer_24 (.in0(A[9]), .in1(A[10]), .out(multiplexer_24_out), .sel(in_2[0]));
  Multiplexer #(.enable("false")) multiplexer_25 (.in0(A[8]), .in1(A[9]), .out(multiplexer_25_out), .sel(in_2[0]));
  Multiplexer #(.enable("false")) multiplexer_26 (.in0(A[7]), .in1(A[8]), .out(multiplexer_26_out), .sel(in_2[0]));
  Multiplexer #(.enable("false")) multiplexer_27 (.in0(A[6]), .in1(A[7]), .out(multiplexer_27_out), .sel(in_2[0]));
  Multiplexer #(.enable("false")) multiplexer_28 (.in0(A[5]), .in1(A[6]), .out(multiplexer_28_out), .sel(in_2[0]));
  Multiplexer #(.enable("false")) multiplexer_29 (.in0(A[4]), .in1(A[5]), .out(multiplexer_29_out), .sel(in_2[0]));
  Multiplexer #(.enable("false")) multiplexer_30 (.in0(A[3]), .in1(A[4]), .out(multiplexer_30_out), .sel(in_2[0]));
  Multiplexer #(.enable("false")) multiplexer_31 (.in0(A[2]), .in1(A[3]), .out(multiplexer_31_out), .sel(in_2[0]));
  Multiplexer #(.enable("false")) multiplexer_32 (.in0(A[1]), .in1(A[2]), .out(multiplexer_32_out), .sel(in_2[0]));
  Multiplexer #(.enable("false")) multiplexer_33 (.in0(A[0]), .in1(A[1]), .out(multiplexer_33_out), .sel(in_2[0]));
  Multiplexer #(.enable("false")) multiplexer_34 (
    .in0(multiplexer_2_out), .in1(A[31]), .out(multiplexer_34_out), .sel(in_2[1]));
  Multiplexer #(.enable("false")) multiplexer_35 (
    .in0(multiplexer_3_out), .in1(A[31]), .out(multiplexer_35_out), .sel(in_2[1]));
  Multiplexer #(.enable("false")) multiplexer_36 (
    .in0(multiplexer_4_out), .in1(multiplexer_2_out), .out(multiplexer_36_out), .sel(in_2[1]));
  Multiplexer #(.enable("false")) multiplexer_37 (
    .in0(multiplexer_5_out), .in1(multiplexer_3_out), .out(multiplexer_37_out), .sel(in_2[1]));
  Multiplexer #(.enable("false")) multiplexer_38 (
    .in0(multiplexer_6_out), .in1(multiplexer_4_out), .out(multiplexer_38_out), .sel(in_2[1]));
  Multiplexer #(.enable("false")) multiplexer_39 (
    .in0(multiplexer_7_out), .in1(multiplexer_5_out), .out(multiplexer_39_out), .sel(in_2[1]));
  Multiplexer #(.enable("false")) multiplexer_40 (
    .in0(multiplexer_8_out), .in1(multiplexer_6_out), .out(multiplexer_40_out), .sel(in_2[1]));
  Multiplexer #(.enable("false")) multiplexer_41 (
    .in0(multiplexer_9_out), .in1(multiplexer_7_out), .out(multiplexer_41_out), .sel(in_2[1]));
  Multiplexer #(.enable("false")) multiplexer_42 (
    .in0(multiplexer_10_out), .in1(multiplexer_8_out), .out(multiplexer_42_out), .sel(in_2[1]));
  Multiplexer #(.enable("false")) multiplexer_43 (
    .in0(multiplexer_11_out), .in1(multiplexer_9_out), .out(multiplexer_43_out), .sel(in_2[1]));
  Multiplexer #(.enable("false")) multiplexer_44 (
    .in0(multiplexer_12_out), .in1(multiplexer_10_out), .out(multiplexer_44_out), .sel(in_2[1]));
  Multiplexer #(.enable("false")) multiplexer_45 (
    .in0(multiplexer_13_out), .in1(multiplexer_11_out), .out(multiplexer_45_out), .sel(in_2[1]));
  Multiplexer #(.enable("false")) multiplexer_46 (
    .in0(multiplexer_14_out), .in1(multiplexer_12_out), .out(multiplexer_46_out), .sel(in_2[1]));
  Multiplexer #(.enable("false")) multiplexer_47 (
    .in0(multiplexer_15_out), .in1(multiplexer_13_out), .out(multiplexer_47_out), .sel(in_2[1]));
  Multiplexer #(.enable("false")) multiplexer_48 (
    .in0(multiplexer_16_out), .in1(multiplexer_14_out), .out(multiplexer_48_out), .sel(in_2[1]));
  Multiplexer #(.enable("false")) multiplexer_49 (
    .in0(multiplexer_17_out), .in1(multiplexer_15_out), .out(multiplexer_49_out), .sel(in_2[1]));
  Multiplexer #(.enable("false")) multiplexer_50 (
    .in0(multiplexer_18_out), .in1(multiplexer_16_out), .out(multiplexer_50_out), .sel(in_2[1]));
  Multiplexer #(.enable("false")) multiplexer_51 (
    .in0(multiplexer_19_out), .in1(multiplexer_17_out), .out(multiplexer_51_out), .sel(in_2[1]));
  Multiplexer #(.enable("false")) multiplexer_52 (
    .in0(multiplexer_20_out), .in1(multiplexer_18_out), .out(multiplexer_52_out), .sel(in_2[1]));
  Multiplexer #(.enable("false")) multiplexer_53 (
    .in0(multiplexer_21_out), .in1(multiplexer_19_out), .out(multiplexer_53_out), .sel(in_2[1]));
  Multiplexer #(.enable("false")) multiplexer_54 (
    .in0(multiplexer_22_out), .in1(multiplexer_20_out), .out(multiplexer_54_out), .sel(in_2[1]));
  Multiplexer #(.enable("false")) multiplexer_55 (
    .in0(multiplexer_23_out), .in1(multiplexer_21_out), .out(multiplexer_55_out), .sel(in_2[1]));
  Multiplexer #(.enable("false")) multiplexer_56 (
    .in0(multiplexer_24_out), .in1(multiplexer_22_out), .out(multiplexer_56_out), .sel(in_2[1]));
  Multiplexer #(.enable("false")) multiplexer_57 (
    .in0(multiplexer_25_out), .in1(multiplexer_23_out), .out(multiplexer_57_out), .sel(in_2[1]));
  Multiplexer #(.enable("false")) multiplexer_58 (
    .in0(multiplexer_26_out), .in1(multiplexer_24_out), .out(multiplexer_58_out), .sel(in_2[1]));
  Multiplexer #(.enable("false")) multiplexer_59 (
    .in0(multiplexer_27_out), .in1(multiplexer_25_out), .out(multiplexer_59_out), .sel(in_2[1]));
  Multiplexer #(.enable("false")) multiplexer_60 (
    .in0(multiplexer_28_out), .in1(multiplexer_26_out), .out(multiplexer_60_out), .sel(in_2[1]));
  Multiplexer #(.enable("false")) multiplexer_61 (
    .in0(multiplexer_29_out), .in1(multiplexer_27_out), .out(multiplexer_61_out), .sel(in_2[1]));
  Multiplexer #(.enable("false")) multiplexer_62 (
    .in0(multiplexer_30_out), .in1(multiplexer_28_out), .out(multiplexer_62_out), .sel(in_2[1]));
  Multiplexer #(.enable("false")) multiplexer_63 (
    .in0(multiplexer_31_out), .in1(multiplexer_29_out), .out(multiplexer_63_out), .sel(in_2[1]));
  Multiplexer #(.enable("false")) multiplexer_64 (
    .in0(multiplexer_32_out), .in1(multiplexer_30_out), .out(multiplexer_64_out), .sel(in_2[1]));
  Multiplexer #(.enable("false")) multiplexer_65 (
    .in0(multiplexer_33_out), .in1(multiplexer_31_out), .out(multiplexer_65_out), .sel(in_2[1]));
  Multiplexer #(.enable("false")) multiplexer_66 (
    .in0(multiplexer_34_out), .in1(A[31]), .out(multiplexer_66_out), .sel(in_2[2]));
  Multiplexer #(.enable("false")) multiplexer_67 (
    .in0(multiplexer_35_out), .in1(A[31]), .out(multiplexer_67_out), .sel(in_2[2]));
  Multiplexer #(.enable("false")) multiplexer_68 (
    .in0(multiplexer_36_out), .in1(A[31]), .out(multiplexer_68_out), .sel(in_2[2]));
  Multiplexer #(.enable("false")) multiplexer_69 (
    .in0(multiplexer_37_out), .in1(A[31]), .out(multiplexer_69_out), .sel(in_2[2]));
  Multiplexer #(.enable("false")) multiplexer_70 (
    .in0(multiplexer_38_out), .in1(multiplexer_34_out), .out(multiplexer_70_out), .sel(in_2[2]));
  Multiplexer #(.enable("false")) multiplexer_71 (
    .in0(multiplexer_39_out), .in1(multiplexer_35_out), .out(multiplexer_71_out), .sel(in_2[2]));
  Multiplexer #(.enable("false")) multiplexer_72 (
    .in0(multiplexer_40_out), .in1(multiplexer_36_out), .out(multiplexer_72_out), .sel(in_2[2]));
  Multiplexer #(.enable("false")) multiplexer_73 (
    .in0(multiplexer_41_out), .in1(multiplexer_37_out), .out(multiplexer_73_out), .sel(in_2[2]));
  Multiplexer #(.enable("false")) multiplexer_74 (
    .in0(multiplexer_42_out), .in1(multiplexer_38_out), .out(multiplexer_74_out), .sel(in_2[2]));
  Multiplexer #(.enable("false")) multiplexer_75 (
    .in0(multiplexer_43_out), .in1(multiplexer_39_out), .out(multiplexer_75_out), .sel(in_2[2]));
  Multiplexer #(.enable("false")) multiplexer_76 (
    .in0(multiplexer_44_out), .in1(multiplexer_40_out), .out(multiplexer_76_out), .sel(in_2[2]));
  Multiplexer #(.enable("false")) multiplexer_77 (
    .in0(multiplexer_45_out), .in1(multiplexer_41_out), .out(multiplexer_77_out), .sel(in_2[2]));
  Multiplexer #(.enable("false")) multiplexer_78 (
    .in0(multiplexer_46_out), .in1(multiplexer_42_out), .out(multiplexer_78_out), .sel(in_2[2]));
  Multiplexer #(.enable("false")) multiplexer_79 (
    .in0(multiplexer_47_out), .in1(multiplexer_43_out), .out(multiplexer_79_out), .sel(in_2[2]));
  Multiplexer #(.enable("false")) multiplexer_80 (
    .in0(multiplexer_48_out), .in1(multiplexer_44_out), .out(multiplexer_80_out), .sel(in_2[2]));
  Multiplexer #(.enable("false")) multiplexer_81 (
    .in0(multiplexer_49_out), .in1(multiplexer_45_out), .out(multiplexer_81_out), .sel(in_2[2]));
  Multiplexer #(.enable("false")) multiplexer_82 (
    .in0(multiplexer_50_out), .in1(multiplexer_46_out), .out(multiplexer_82_out), .sel(in_2[2]));
  Multiplexer #(.enable("false")) multiplexer_83 (
    .in0(multiplexer_51_out), .in1(multiplexer_47_out), .out(multiplexer_83_out), .sel(in_2[2]));
  Multiplexer #(.enable("false")) multiplexer_84 (
    .in0(multiplexer_52_out), .in1(multiplexer_48_out), .out(multiplexer_84_out), .sel(in_2[2]));
  Multiplexer #(.enable("false")) multiplexer_85 (
    .in0(multiplexer_53_out), .in1(multiplexer_49_out), .out(multiplexer_85_out), .sel(in_2[2]));
  Multiplexer #(.enable("false")) multiplexer_86 (
    .in0(multiplexer_54_out), .in1(multiplexer_50_out), .out(multiplexer_86_out), .sel(in_2[2]));
  Multiplexer #(.enable("false")) multiplexer_87 (
    .in0(multiplexer_55_out), .in1(multiplexer_51_out), .out(multiplexer_87_out), .sel(in_2[2]));
  Multiplexer #(.enable("false")) multiplexer_88 (
    .in0(multiplexer_56_out), .in1(multiplexer_52_out), .out(multiplexer_88_out), .sel(in_2[2]));
  Multiplexer #(.enable("false")) multiplexer_89 (
    .in0(multiplexer_57_out), .in1(multiplexer_53_out), .out(multiplexer_89_out), .sel(in_2[2]));
  Multiplexer #(.enable("false")) multiplexer_90 (
    .in0(multiplexer_58_out), .in1(multiplexer_54_out), .out(multiplexer_90_out), .sel(in_2[2]));
  Multiplexer #(.enable("false")) multiplexer_91 (
    .in0(multiplexer_59_out), .in1(multiplexer_55_out), .out(multiplexer_91_out), .sel(in_2[2]));
  Multiplexer #(.enable("false")) multiplexer_92 (
    .in0(multiplexer_60_out), .in1(multiplexer_56_out), .out(multiplexer_92_out), .sel(in_2[2]));
  Multiplexer #(.enable("false")) multiplexer_93 (
    .in0(multiplexer_61_out), .in1(multiplexer_57_out), .out(multiplexer_93_out), .sel(in_2[2]));
  Multiplexer #(.enable("false")) multiplexer_94 (
    .in0(multiplexer_62_out), .in1(multiplexer_58_out), .out(multiplexer_94_out), .sel(in_2[2]));
  Multiplexer #(.enable("false")) multiplexer_95 (
    .in0(multiplexer_63_out), .in1(multiplexer_59_out), .out(multiplexer_95_out), .sel(in_2[2]));
  Multiplexer #(.enable("false")) multiplexer_96 (
    .in0(multiplexer_64_out), .in1(multiplexer_60_out), .out(multiplexer_96_out), .sel(in_2[2]));
  Multiplexer #(.enable("false")) multiplexer_97 (
    .in0(multiplexer_65_out), .in1(multiplexer_61_out), .out(multiplexer_97_out), .sel(in_2[2]));
  Multiplexer #(.enable("false")) multiplexer_98 (
    .in0(multiplexer_66_out), .in1(A[31]), .out(multiplexer_98_out), .sel(in_2[3]));
  Multiplexer #(.enable("false")) multiplexer_99 (
    .in0(multiplexer_67_out), .in1(A[31]), .out(multiplexer_99_out), .sel(in_2[3]));
  Multiplexer #(.enable("false")) multiplexer_100 (
    .in0(multiplexer_68_out), .in1(A[31]), .out(multiplexer_100_out), .sel(in_2[3]));
  Multiplexer #(.enable("false")) multiplexer_101 (
    .in0(multiplexer_69_out), .in1(A[31]), .out(multiplexer_101_out), .sel(in_2[3]));
  Multiplexer #(.enable("false")) multiplexer_102 (
    .in0(multiplexer_70_out), .in1(A[31]), .out(multiplexer_102_out), .sel(in_2[3]));
  Multiplexer #(.enable("false")) multiplexer_103 (
    .in0(multiplexer_71_out), .in1(A[31]), .out(multiplexer_103_out), .sel(in_2[3]));
  Multiplexer #(.enable("false")) multiplexer_104 (
    .in0(multiplexer_72_out), .in1(A[31]), .out(multiplexer_104_out), .sel(in_2[3]));
  Multiplexer #(.enable("false")) multiplexer_105 (
    .in0(multiplexer_73_out), .in1(A[31]), .out(multiplexer_105_out), .sel(in_2[3]));
  Multiplexer #(.enable("false")) multiplexer_106 (
    .in0(multiplexer_74_out), .in1(multiplexer_66_out), .out(multiplexer_106_out), .sel(in_2[3]));
  Multiplexer #(.enable("false")) multiplexer_107 (
    .in0(multiplexer_75_out), .in1(multiplexer_67_out), .out(multiplexer_107_out), .sel(in_2[3]));
  Multiplexer #(.enable("false")) multiplexer_108 (
    .in0(multiplexer_76_out), .in1(multiplexer_68_out), .out(multiplexer_108_out), .sel(in_2[3]));
  Multiplexer #(.enable("false")) multiplexer_109 (
    .in0(multiplexer_77_out), .in1(multiplexer_69_out), .out(multiplexer_109_out), .sel(in_2[3]));
  Multiplexer #(.enable("false")) multiplexer_110 (
    .in0(multiplexer_78_out), .in1(multiplexer_70_out), .out(multiplexer_110_out), .sel(in_2[3]));
  Multiplexer #(.enable("false")) multiplexer_111 (
    .in0(multiplexer_79_out), .in1(multiplexer_71_out), .out(multiplexer_111_out), .sel(in_2[3]));
  Multiplexer #(.enable("false")) multiplexer_112 (
    .in0(multiplexer_80_out), .in1(multiplexer_72_out), .out(multiplexer_112_out), .sel(in_2[3]));
  Multiplexer #(.enable("false")) multiplexer_113 (
    .in0(multiplexer_81_out), .in1(multiplexer_73_out), .out(multiplexer_113_out), .sel(in_2[3]));
  Multiplexer #(.enable("false")) multiplexer_114 (
    .in0(multiplexer_82_out), .in1(multiplexer_74_out), .out(multiplexer_114_out), .sel(in_2[3]));
  Multiplexer #(.enable("false")) multiplexer_115 (
    .in0(multiplexer_83_out), .in1(multiplexer_75_out), .out(multiplexer_115_out), .sel(in_2[3]));
  Multiplexer #(.enable("false")) multiplexer_116 (
    .in0(multiplexer_84_out), .in1(multiplexer_76_out), .out(multiplexer_116_out), .sel(in_2[3]));
  Multiplexer #(.enable("false")) multiplexer_117 (
    .in0(multiplexer_85_out), .in1(multiplexer_77_out), .out(multiplexer_117_out), .sel(in_2[3]));
  Multiplexer #(.enable("false")) multiplexer_118 (
    .in0(multiplexer_86_out), .in1(multiplexer_78_out), .out(multiplexer_118_out), .sel(in_2[3]));
  Multiplexer #(.enable("false")) multiplexer_119 (
    .in0(multiplexer_87_out), .in1(multiplexer_79_out), .out(multiplexer_119_out), .sel(in_2[3]));
  Multiplexer #(.enable("false")) multiplexer_120 (
    .in0(multiplexer_88_out), .in1(multiplexer_80_out), .out(multiplexer_120_out), .sel(in_2[3]));
  Multiplexer #(.enable("false")) multiplexer_121 (
    .in0(multiplexer_89_out), .in1(multiplexer_81_out), .out(multiplexer_121_out), .sel(in_2[3]));
  Multiplexer #(.enable("false")) multiplexer_122 (
    .in0(multiplexer_90_out), .in1(multiplexer_82_out), .out(multiplexer_122_out), .sel(in_2[3]));
  Multiplexer #(.enable("false")) multiplexer_123 (
    .in0(multiplexer_91_out), .in1(multiplexer_83_out), .out(multiplexer_123_out), .sel(in_2[3]));
  Multiplexer #(.enable("false")) multiplexer_124 (
    .in0(multiplexer_92_out), .in1(multiplexer_84_out), .out(multiplexer_124_out), .sel(in_2[3]));
  Multiplexer #(.enable("false")) multiplexer_125 (
    .in0(multiplexer_93_out), .in1(multiplexer_85_out), .out(multiplexer_125_out), .sel(in_2[3]));
  Multiplexer #(.enable("false")) multiplexer_126 (
    .in0(multiplexer_94_out), .in1(multiplexer_86_out), .out(multiplexer_126_out), .sel(in_2[3]));
  Multiplexer #(.enable("false")) multiplexer_127 (
    .in0(multiplexer_95_out), .in1(multiplexer_87_out), .out(multiplexer_127_out), .sel(in_2[3]));
  Multiplexer #(.enable("false")) multiplexer_128 (
    .in0(multiplexer_96_out), .in1(multiplexer_88_out), .out(multiplexer_128_out), .sel(in_2[3]));
  Multiplexer #(.enable("false")) multiplexer_129 (
    .in0(multiplexer_97_out), .in1(multiplexer_89_out), .out(multiplexer_129_out), .sel(in_2[3]));
  Multiplexer #(.enable("false")) multiplexer_130 (.in0(multiplexer_98_out), .in1(A[31]), .out(O1), .sel(in_2[4]));
  Multiplexer #(.enable("false")) multiplexer_131 (.in0(multiplexer_99_out), .in1(A[31]), .out(O2), .sel(in_2[4]));
  Multiplexer #(.enable("false")) multiplexer_132 (.in0(multiplexer_100_out), .in1(A[31]), .out(O3), .sel(in_2[4]));
  Multiplexer #(.enable("false")) multiplexer_133 (.in0(multiplexer_101_out), .in1(A[31]), .out(O4), .sel(in_2[4]));
  Multiplexer #(.enable("false")) multiplexer_134 (.in0(multiplexer_102_out), .in1(A[31]), .out(O5), .sel(in_2[4]));
  Multiplexer #(.enable("false")) multiplexer_135 (.in0(multiplexer_103_out), .in1(A[31]), .out(O6), .sel(in_2[4]));
  Multiplexer #(.enable("false")) multiplexer_136 (.in0(multiplexer_104_out), .in1(A[31]), .out(O7), .sel(in_2[4]));
  Multiplexer #(.enable("false")) multiplexer_137 (.in0(multiplexer_105_out), .in1(A[31]), .out(O8), .sel(in_2[4]));
  Multiplexer #(.enable("false")) multiplexer_138 (.in0(multiplexer_106_out), .in1(A[31]), .out(O9), .sel(in_2[4]));
  Multiplexer #(.enable("false")) multiplexer_139 (.in0(multiplexer_107_out), .in1(A[31]), .out(O10), .sel(in_2[4]));
  Multiplexer #(.enable("false")) multiplexer_140 (.in0(multiplexer_108_out), .in1(A[31]), .out(O11), .sel(in_2[4]));
  Multiplexer #(.enable("false")) multiplexer_141 (.in0(multiplexer_109_out), .in1(A[31]), .out(O12), .sel(in_2[4]));
  Multiplexer #(.enable("false")) multiplexer_142 (.in0(multiplexer_110_out), .in1(A[31]), .out(O13), .sel(in_2[4]));
  Multiplexer #(.enable("false")) multiplexer_143 (.in0(multiplexer_111_out), .in1(A[31]), .out(O14), .sel(in_2[4]));
  Multiplexer #(.enable("false")) multiplexer_144 (.in0(multiplexer_112_out), .in1(A[31]), .out(O15), .sel(in_2[4]));
  Multiplexer #(.enable("false")) multiplexer_145 (.in0(multiplexer_113_out), .in1(A[31]), .out(O16), .sel(in_2[4]));
  Multiplexer #(.enable("false")) multiplexer_146 (
    .in0(multiplexer_114_out), .in1(multiplexer_98_out), .out(O17), .sel(in_2[4]));
  Multiplexer #(.enable("false")) multiplexer_147 (
    .in0(multiplexer_115_out), .in1(multiplexer_99_out), .out(O18), .sel(in_2[4]));
  Multiplexer #(.enable("false")) multiplexer_148 (
    .in0(multiplexer_116_out), .in1(multiplexer_100_out), .out(O19), .sel(in_2[4]));
  Multiplexer #(.enable("false")) multiplexer_149 (
    .in0(multiplexer_117_out), .in1(multiplexer_101_out), .out(O20), .sel(in_2[4]));
  Multiplexer #(.enable("false")) multiplexer_150 (
    .in0(multiplexer_118_out), .in1(multiplexer_102_out), .out(O21), .sel(in_2[4]));
  Multiplexer #(.enable("false")) multiplexer_151 (
    .in0(multiplexer_119_out), .in1(multiplexer_103_out), .out(O22), .sel(in_2[4]));
  Multiplexer #(.enable("false")) multiplexer_152 (
    .in0(multiplexer_120_out), .in1(multiplexer_104_out), .out(O23), .sel(in_2[4]));
  Multiplexer #(.enable("false")) multiplexer_153 (
    .in0(multiplexer_121_out), .in1(multiplexer_105_out), .out(O24), .sel(in_2[4]));
  Multiplexer #(.enable("false")) multiplexer_154 (
    .in0(multiplexer_122_out), .in1(multiplexer_106_out), .out(O25), .sel(in_2[4]));
  Multiplexer #(.enable("false")) multiplexer_155 (
    .in0(multiplexer_123_out), .in1(multiplexer_107_out), .out(O26), .sel(in_2[4]));
  Multiplexer #(.enable("false")) multiplexer_156 (
    .in0(multiplexer_124_out), .in1(multiplexer_108_out), .out(O27), .sel(in_2[4]));
  Multiplexer #(.enable("false")) multiplexer_157 (
    .in0(multiplexer_125_out), .in1(multiplexer_109_out), .out(O28), .sel(in_2[4]));
  Multiplexer #(.enable("false")) multiplexer_158 (
    .in0(multiplexer_126_out), .in1(multiplexer_110_out), .out(O29), .sel(in_2[4]));
  Multiplexer #(.enable("false")) multiplexer_159 (
    .in0(multiplexer_127_out), .in1(multiplexer_111_out), .out(O30), .sel(in_2[4]));
  Multiplexer #(.enable("false")) multiplexer_160 (
    .in0(multiplexer_128_out), .in1(multiplexer_112_out), .out(O31), .sel(in_2[4]));
  Multiplexer #(.enable("false")) multiplexer_161 (
    .in0(multiplexer_129_out), .in1(multiplexer_113_out), .out(O32), .sel(in_2[4]));

  // Other names for the same wires on the sheet: AA0 = A[0]; AA1 = A[1]; AA2 = A[2]; AA3 = A[3]; AA4 = A[4];
  //   AA5 = A[5]; AA6 = A[6]; AA7 = A[7]; AA8 = A[8]; AA9 = A[9]; AA10 = A[10]; AA11 = A[11]; AA12 = A[12];
  //   AA13 = A[13]; AA14 = A[14]; AA15 = A[15]; AA16 = A[16]; AA17 = A[17]; AA18 = A[18]; AA19 = A[19]; AA20 = A[20];
  //   AA21 = A[21]; AA22 = A[22]; AA23 = A[23]; AA24 = A[24]; AA25 = A[25]; AA26 = A[26]; AA27 = A[27]; AA28 = A[28];
  //   AA29 = A[29]; AA30 = A[30]; AA31 = A[31]; BA0 = in_2[0]; BA1 = in_2[1]; BA2 = in_2[2]; BA3 = in_2[3];
  //   BA4 = in_2[4]
endmodule

module SLL4 (
  input  a3in,
  input  a2in,
  input  a1in,
  input  a0in,
  input  shin,
  input  s0,
  output b3out,
  output b2out,
  output b1out,
  output b0out
);

  Multiplexer #(.enable("false")) multiplexer_1 (.in0(a3in), .in1(a2in), .out(b3out), .sel(s0));
  Multiplexer #(.enable("false")) multiplexer_2 (.in0(a2in), .in1(a1in), .out(b2out), .sel(s0));
  Multiplexer #(.enable("false")) multiplexer_3 (.in0(a1in), .in1(a0in), .out(b1out), .sel(s0));
  Multiplexer #(.enable("false")) multiplexer_4 (.in0(a0in), .in1(shin), .out(b0out), .sel(s0));
endmodule

module shift1 (
  input  [31:0] A,
  output [31:0] shift1out
);

  // SLL4 sll4_1: pin names not known; wires that end beside it: A[31], A[30], A[29], A[28], A[27], shift1out[31], shift1out[30], shift1out[29]
  // SLL4 sll4_2: pin names not known; wires that end beside it: A[27], A[26], A[25], A[24], A[23], shift1out[27], shift1out[26], shift1out[25]
  // SLL4 sll4_3: pin names not known; wires that end beside it: A[23], A[22], A[21], A[20], A[19], shift1out[23], shift1out[22], shift1out[21]
  // SLL4 sll4_4: pin names not known; wires that end beside it: A[19], A[18], A[17], A[16], A[15], shift1out[19], shift1out[18], shift1out[17]
  // SLL4 sll4_5: pin names not known; wires that end beside it: A[15], A[14], A[13], A[12], A[11], shift1out[15], shift1out[14], shift1out[13]
  // SLL4 sll4_6: pin names not known; wires that end beside it: A[11], A[10], A[9], A[8], A[7], shift1out[11], shift1out[10], shift1out[9]
  // SLL4 sll4_7: pin names not known; wires that end beside it: A[7], A[6], A[5], A[4], A[3], shift1out[7], shift1out[6], shift1out[5]
  // SLL4 sll4_8: pin names not known; wires that end beside it: A[3], A[2], A[1], A[0], 1'b0, shift1out[3], shift1out[2], shift1out[1]

  assign {shift1out[28], shift1out[24], shift1out[20], shift1out[16], shift1out[12], shift1out[8], shift1out[4], shift1out[0]} = {8{1'b1}};

  // Other names for the same wires on the sheet: AA0 = A[0]; AA1 = A[1]; AA2 = A[2]; AA3 = A[3]; AA4 = A[4];
  //   AA5 = A[5]; AA6 = A[6]; AA7 = A[7]; AA8 = A[8]; AA9 = A[9]; AA10 = A[10]; AA11 = A[11]; AA12 = A[12];
  //   AA13 = A[13]; AA14 = A[14]; AA15 = A[15]; AA16 = A[16]; AA17 = A[17]; AA18 = A[18]; AA19 = A[19]; AA20 = A[20];
  //   AA21 = A[21]; AA22 = A[22]; AA23 = A[23]; AA24 = A[24]; AA25 = A[25]; AA26 = A[26]; AA27 = A[27]; AA28 = A[28];
  //   AA29 = A[29]; AA30 = A[30]; AA31 = A[31]; o1 = shift1out[1]; o2 = shift1out[2]; o3 = shift1out[3];
  //   o5 = shift1out[5]; o6 = shift1out[6]; o7 = shift1out[7]; o9 = shift1out[9]; o10 = shift1out[10];
  //   o11 = shift1out[11]; o13 = shift1out[13]; o14 = shift1out[14]; o15 = shift1out[15]; o17 = shift1out[17];
  //   o18 = shift1out[18]; o19 = shift1out[19]; o21 = shift1out[21]; o22 = shift1out[22]; o23 = shift1out[23];
  //   o25 = shift1out[25]; o26 = shift1out[26]; o27 = shift1out[27]; o29 = shift1out[29]; o30 = shift1out[30];
  //   o31 = shift1out[31]
endmodule

module overallSLL (
  input  [31:0] A,
  input  [31:0] B,
  output [31:0] shiftOut
);

  wire or_1_out;
  wire [31:0] multiplexer_1_out, shift1_2_shift1out, shift1_3_shift1out, shift1_20_shift1out, shift1mux,
       shift2mux, shift3mux, shift4mux, shift5mux, shift6mux, shift7mux, shift8mux, shift9mux, shift10mux,
       shift11mux, shift12mux, shift13mux, shift14mux, shift15mux, shift16mux, shift17mux, shift18mux,
       shift19mux, shift20mux, shift21mux, shift22mux, shift23mux, shift24mux, shift25mux, shift26mux,
       shift27mux, shift28mux, shift29mux, shift30mux, shift31mux, shift32mux;

  shift1 shift1_1 (.A(A), .shift1out(shift1mux));
  shift1 shift1_2 (.A(A), .shift1out(shift1_2_shift1out));
  shift1 shift1_3 (.A(A), .shift1out(shift1_3_shift1out));
  shift1 shift1_4 (.A(shift3mux), .shift1out(shift4mux));
  shift1 shift1_5 (.A(shift4mux), .shift1out(shift5mux));
  shift1 shift1_6 (.A(shift5mux), .shift1out(shift6mux));
  shift1 shift1_7 (.A(shift6mux), .shift1out(shift7mux));
  shift1 shift1_8 (.A(shift7mux), .shift1out(shift8mux));
  shift1 shift1_9 (.A(shift13mux), .shift1out(shift14mux));
  shift1 shift1_10 (.A(shift14mux), .shift1out(shift15mux));
  shift1 shift1_11 (.A(shift15mux), .shift1out(shift16mux));
  shift1 shift1_12 (.A(shift16mux), .shift1out(shift17mux));
  shift1 shift1_13 (.A(shift17mux), .shift1out(shift18mux));
  shift1 shift1_14 (.A(shift23mux), .shift1out(shift24mux));
  shift1 shift1_15 (.A(shift24mux), .shift1out(shift25mux));
  shift1 shift1_16 (.A(shift25mux), .shift1out(shift26mux));
  shift1 shift1_17 (.A(shift26mux), .shift1out(shift27mux));
  shift1 shift1_18 (.A(shift27mux), .shift1out(shift28mux));
  or or_1 (or_1_out, B[5], B[6], B[7], B[8], B[9], B[10], B[11], B[12], B[13], B[14], B[15], B[16], B[17], B[18], B[19], B[20], B[21], B[22], B[23], B[24], B[25], B[26], B[27], B[28], B[29], B[30], B[31]);
  shift1 shift1_19 (.A(shift1_2_shift1out), .shift1out(shift2mux));
  shift1 shift1_20 (.A(shift1_3_shift1out), .shift1out(shift1_20_shift1out));
  shift1 shift1_21 (.A(shift1_20_shift1out), .shift1out(shift3mux));
  shift1 shift1_22 (.A(shift8mux), .shift1out(shift9mux));
  shift1 shift1_23 (.A(shift9mux), .shift1out(shift10mux));
  shift1 shift1_24 (.A(shift10mux), .shift1out(shift11mux));
  shift1 shift1_25 (.A(shift11mux), .shift1out(shift12mux));
  shift1 shift1_26 (.A(shift12mux), .shift1out(shift13mux));
  shift1 shift1_27 (.A(shift18mux), .shift1out(shift19mux));
  shift1 shift1_28 (.A(shift19mux), .shift1out(shift20mux));
  shift1 shift1_29 (.A(shift20mux), .shift1out(shift21mux));
  shift1 shift1_30 (.A(shift21mux), .shift1out(shift22mux));
  shift1 shift1_31 (.A(shift22mux), .shift1out(shift23mux));
  shift1 shift1_32 (.A(shift28mux), .shift1out(shift29mux));
  shift1 shift1_33 (.A(shift29mux), .shift1out(shift30mux));
  shift1 shift1_34 (.A(shift30mux), .shift1out(shift31mux));
  shift1 shift1_35 (.A(shift31mux), .shift1out(shift32mux));
  Multiplexer #(.select(5), .width(32), .enable("false")) multiplexer_1 (
    .in0(A), .in1(shift1mux), .in2(shift2mux), .in3(shift3mux), .in4(shift4mux), .in5(shift5mux),
    .in6(shift6mux), .in7(shift7mux), .in8(shift8mux), .in9(shift9mux), .in10(shift10mux), .in11(shift11mux),
    .in12(shift12mux), .in13(shift13mux), .in14(shift14mux), .in15(shift15mux), .in16(shift16mux),
    .in17(shift17mux), .in18(shift18mux), .in19(shift19mux), .in20(shift20mux), .in21(shift21mux),
    .in22(shift22mux), .in23(shift23mux), .in24(shift24mux), .in25(shift25mux), .in26(shift26mux),
    .in27(shift27mux), .in28(shift28mux), .in29(shift29mux), .in30(shift30mux), .in31(shift31mux),
    .out(multiplexer_1_out), .sel(B[4:0]));
  Multiplexer #(.width(32), .enable("false")) multiplexer_2 (
    .in0(multiplexer_1_out), .in1({32{1'b0}}), .out(shiftOut), .sel(or_1_out));

  // Other names for the same wires on the sheet: B_5Bit[4:0] = B[4:0]; BA0 = B[0]; BA1 = B[1]; BA2 = B[2]; BA3 = B[3];
  //   BA4 = B[4]; A_IN[31:0] = A; shift0mux[31:0] = A
endmodule

module overallSubtract (
  input  [31:0] A,
  input  [31:0] B,
  output [31:0] subtractOut
);

  wire [31:0] overalladd_2_addout, xor_1_out;

  assign xor_1_out = B ^ {32{1'b1}};  // XOR_Gate xor_1, 32 bits wide
  overallAdd overalladd_1 (.A(A), .B(overalladd_2_addout), .addOut(subtractOut));
  overallAdd overalladd_2 (.A(32'h1), .B(xor_1_out), .addOut(overalladd_2_addout));
endmodule

module overallSLT (
  input  [31:0] A,
  input  [31:0] B,
  output [31:0] SLTout
);

  wire [30:0] overallsubtract_1_subtractout;

  overallSubtract overallsubtract_1 (.A(A), .B(B), .subtractOut({SLTout[0], overallsubtract_1_subtractout}));

  assign SLTout[31:1] = {31{1'b0}};
endmodule

module pc (
);

  wire clk;
  wire [31:0] overalladd_1_addout, PROGRAM_COUNTER;

  overallAdd overalladd_1 (.A(PROGRAM_COUNTER), .B(32'h4), .addOut(overalladd_1_addout));
  Register #(.width(32), .trigger("falling")) register_1 (
    .D(overalladd_1_addout), .clk(clk), .Q(PROGRAM_COUNTER));  // open: en, clr
endmodule
