// Logisim project branch_comp.circ as structural Verilog: 4 circuits, main circuit branch_comp
module branch_comp (
  input  [31:0] rs1,
  input  [31:0] rs2,
  input  BrUn,
  output BrEq,
  output BrLt,
  output out_6
);

  wire undriven, undriven_2, undriven_3, undriven_4, undriven_5;
  wire [30:0] sub_1_out_3;

  sub sub_1 (.in_1(rs1), .in_2(rs2), .out_3({BrLt, sub_1_out_3}));
  or or_1 (BrEq, sub_1_out_3[0], sub_1_out_3[1], sub_1_out_3[2], sub_1_out_3[3], sub_1_out_3[4], sub_1_out_3[5], sub_1_out_3[6], sub_1_out_3[7], sub_1_out_3[8], sub_1_out_3[9], sub_1_out_3[10], sub_1_out_3[11], sub_1_out_3[12], sub_1_out_3[13], sub_1_out_3[14], sub_1_out_3[15], sub_1_out_3[16], sub_1_out_3[17], sub_1_out_3[18], sub_1_out_3[19], sub_1_out_3[20], sub_1_out_3[21], sub_1_out_3[22], sub_1_out_3[23], sub_1_out_3[24], sub_1_out_3[25], sub_1_out_3[26], sub_1_out_3[27], sub_1_out_3[28], sub_1_out_3[29], sub_1_out_3[30], BrLt);
  Multiplexer #(.enable("false")) multiplexer_1 (.in0(undriven), .in1(undriven_3), .sel(undriven_5));  // open: out
  Multiplexer #(.enable("false")) multiplexer_2 (.in0(undriven_2), .in1(undriven_4), .sel(undriven_5));  // open: out

  assign out_6 = BrEq;

  // Notes on the sheet:
  //   INPUTS to your circuit
  //   DON'T CHANGE THE LOCATIONS OF THE INPUTS AND OUTPUTS!
  //   OUTPUT from your circuit
endmodule

module sub (
  input  [31:0] in_1,
  input  [31:0] in_2,
  output [31:0] out_3
);

  wire [31:0] add_2_out_3, xor_1_out;

  assign xor_1_out = in_2 ^ {32{1'b1}};  // XOR_Gate xor_1, 32 bits wide
  add add_1 (.in_1(in_1), .in_2(add_2_out_3), .out_3(out_3));
  add add_2 (.in_1(32'h1), .in_2(xor_1_out), .out_3(add_2_out_3));
endmodule

module add (
  input  [31:0] in_1,
  input  [31:0] in_2,
  output [31:0] out_3
);

  wire addercirc_1_out_5, addercirc_2_out_5, addercirc_3_out_5, addercirc_4_out_5, addercirc_5_out_5,
       addercirc_6_out_5, addercirc_7_out_5, addercirc_8_out_5, addercirc_9_out_5, addercirc_10_out_5,
       addercirc_11_out_5, addercirc_12_out_5, addercirc_13_out_5, addercirc_14_out_5, addercirc_15_out_5,
       addercirc_16_out_5, addercirc_17_out_5, addercirc_18_out_5, addercirc_19_out_5, addercirc_20_out_5,
       addercirc_21_out_5, addercirc_22_out_5, addercirc_23_out_5, addercirc_24_out_5, addercirc_25_out_5,
       addercirc_26_out_5, addercirc_27_out_5, addercirc_28_out_5, addercirc_29_out_5, addercirc_30_out_5,
       addercirc_31_out_5;

  adderCirc addercirc_1 (.out_5(addercirc_1_out_5), .in_3(1'b0), .out_4(out_3[0]), .in_2(in_2[0]), .in_1(in_1[0]));
  adderCirc addercirc_2 (
    .out_5(addercirc_2_out_5), .in_3(addercirc_1_out_5), .out_4(out_3[1]), .in_2(in_2[1]), .in_1(in_1[1]));
  adderCirc addercirc_3 (
    .out_5(addercirc_3_out_5), .in_3(addercirc_2_out_5), .out_4(out_3[2]), .in_2(in_2[2]), .in_1(in_1[2]));
  adderCirc addercirc_4 (
    .out_5(addercirc_4_out_5), .in_3(addercirc_3_out_5), .out_4(out_3[3]), .in_2(in_2[3]), .in_1(in_1[3]));
  adderCirc addercirc_5 (
    .out_5(addercirc_5_out_5), .in_3(addercirc_4_out_5), .out_4(out_3[4]), .in_2(in_2[4]), .in_1(in_1[4]));
  adderCirc addercirc_6 (
    .out_5(addercirc_6_out_5), .in_3(addercirc_5_out_5), .out_4(out_3[5]), .in_2(in_2[5]), .in_1(in_1[5]));
  adderCirc addercirc_7 (
    .out_5(addercirc_7_out_5), .in_3(addercirc_6_out_5), .out_4(out_3[6]), .in_2(in_2[6]), .in_1(in_1[6]));
  adderCirc addercirc_8 (
    .out_5(addercirc_8_out_5), .in_3(addercirc_7_out_5), .out_4(out_3[7]), .in_2(in_2[7]), .in_1(in_1[7]));
  adderCirc addercirc_9 (
    .out_5(addercirc_9_out_5), .in_3(addercirc_8_out_5), .out_4(out_3[8]), .in_2(in_2[8]), .in_1(in_1[8]));
  adderCirc addercirc_10 (
    .out_5(addercirc_10_out_5), .in_3(addercirc_9_out_5), .out_4(out_3[9]), .in_2(in_2[9]), .in_1(in_1[9]));
  adderCirc addercirc_11 (
    .out_5(addercirc_11_out_5), .in_3(addercirc_10_out_5), .out_4(out_3[10]), .in_2(in_2[10]), .in_1(in_1[10]));
  adderCirc addercirc_12 (
    .out_5(addercirc_12_out_5), .in_3(addercirc_11_out_5), .out_4(out_3[11]), .in_2(in_2[11]), .in_1(in_1[11]));
  adderCirc addercirc_13 (
    .out_5(addercirc_13_out_5), .in_3(addercirc_12_out_5), .out_4(out_3[12]), .in_2(in_2[12]), .in_1(in_1[12]));
  adderCirc addercirc_14 (
    .out_5(addercirc_14_out_5), .in_3(addercirc_13_out_5), .out_4(out_3[13]), .in_2(in_2[13]), .in_1(in_1[13]));
  adderCirc addercirc_15 (
    .out_5(addercirc_15_out_5), .in_3(addercirc_14_out_5), .out_4(out_3[14]), .in_2(in_2[14]), .in_1(in_1[14]));
  adderCirc addercirc_16 (
    .out_5(addercirc_16_out_5), .in_3(addercirc_15_out_5), .out_4(out_3[15]), .in_2(in_2[15]), .in_1(in_1[15]));
  adderCirc addercirc_17 (
    .out_5(addercirc_17_out_5), .in_3(addercirc_16_out_5), .out_4(out_3[16]), .in_2(in_2[16]), .in_1(in_1[16]));
  adderCirc addercirc_18 (
    .out_5(addercirc_18_out_5), .in_3(addercirc_17_out_5), .out_4(out_3[17]), .in_2(in_2[17]), .in_1(in_1[17]));
  adderCirc addercirc_19 (
    .out_5(addercirc_19_out_5), .in_3(addercirc_18_out_5), .out_4(out_3[18]), .in_2(in_2[18]), .in_1(in_1[18]));
  adderCirc addercirc_20 (
    .out_5(addercirc_20_out_5), .in_3(addercirc_19_out_5), .out_4(out_3[19]), .in_2(in_2[19]), .in_1(in_1[19]));
  adderCirc addercirc_21 (
    .out_5(addercirc_21_out_5), .in_3(addercirc_20_out_5), .out_4(out_3[20]), .in_2(in_2[20]), .in_1(in_1[20]));
  adderCirc addercirc_22 (
    .out_5(addercirc_22_out_5), .in_3(addercirc_21_out_5), .out_4(out_3[21]), .in_2(in_2[21]), .in_1(in_1[21]));
  adderCirc addercirc_23 (
    .out_5(addercirc_23_out_5), .in_3(addercirc_22_out_5), .out_4(out_3[22]), .in_2(in_2[22]), .in_1(in_1[22]));
  adderCirc addercirc_24 (
    .out_5(addercirc_24_out_5), .in_3(addercirc_23_out_5), .out_4(out_3[23]), .in_2(in_2[23]), .in_1(in_1[23]));
  adderCirc addercirc_25 (
    .out_5(addercirc_25_out_5), .in_3(addercirc_24_out_5), .out_4(out_3[24]), .in_2(in_2[24]), .in_1(in_1[24]));
  adderCirc addercirc_26 (
    .out_5(addercirc_26_out_5), .in_3(addercirc_25_out_5), .out_4(out_3[25]), .in_2(in_2[25]), .in_1(in_1[25]));
  adderCirc addercirc_27 (
    .out_5(addercirc_27_out_5), .in_3(addercirc_26_out_5), .out_4(out_3[26]), .in_2(in_2[26]), .in_1(in_1[26]));
  adderCirc addercirc_28 (
    .out_5(addercirc_28_out_5), .in_3(addercirc_27_out_5), .out_4(out_3[27]), .in_2(in_2[27]), .in_1(in_1[27]));
  adderCirc addercirc_29 (
    .out_5(addercirc_29_out_5), .in_3(addercirc_28_out_5), .out_4(out_3[28]), .in_2(in_2[28]), .in_1(in_1[28]));
  adderCirc addercirc_30 (
    .out_5(addercirc_30_out_5), .in_3(addercirc_29_out_5), .out_4(out_3[29]), .in_2(in_2[29]), .in_1(in_1[29]));
  adderCirc addercirc_31 (
    .out_5(addercirc_31_out_5), .in_3(addercirc_30_out_5), .out_4(out_3[30]), .in_2(in_2[30]), .in_1(in_1[30]));
  adderCirc addercirc_32 (
    .in_3(addercirc_31_out_5), .out_4(out_3[31]), .in_2(in_2[31]), .in_1(in_1[31]));  // open: out_5

  // Other names for the same wires on the sheet: AA0 = in_1[0]; AA1 = in_1[1]; AA2 = in_1[2]; AA3 = in_1[3];
  //   AA4 = in_1[4]; AA5 = in_1[5]; AA6 = in_1[6]; AA7 = in_1[7]; AA8 = in_1[8]; AA9 = in_1[9]; AA10 = in_1[10];
  //   AA11 = in_1[11]; AA12 = in_1[12]; AA13 = in_1[13]; AA14 = in_1[14]; AA15 = in_1[15]; AA16 = in_1[16];
  //   AA17 = in_1[17]; AA18 = in_1[18]; AA19 = in_1[19]; AA20 = in_1[20]; AA21 = in_1[21]; AA22 = in_1[22];
  //   AA23 = in_1[23]; AA24 = in_1[24]; AA25 = in_1[25]; AA26 = in_1[26]; AA27 = in_1[27]; AA28 = in_1[28];
  //   AA29 = in_1[29]; AA30 = in_1[30]; AA31 = in_1[31]; BA0 = in_2[0]; BA1 = in_2[1]; BA2 = in_2[2]; BA3 = in_2[3];
  //   BA4 = in_2[4]; BA5 = in_2[5]; BA6 = in_2[6]; BA7 = in_2[7]; BA8 = in_2[8]; BA9 = in_2[9]; BA10 = in_2[10];
  //   BA11 = in_2[11]; BA12 = in_2[12]; BA13 = in_2[13]; BA14 = in_2[14]; BA15 = in_2[15]; BA16 = in_2[16];
  //   BA17 = in_2[17]; BA18 = in_2[18]; BA19 = in_2[19]; BA20 = in_2[20]; BA21 = in_2[21]; BA22 = in_2[22];
  //   BA23 = in_2[23]; BA24 = in_2[24]; BA25 = in_2[25]; BA26 = in_2[26]; BA27 = in_2[27]; BA28 = in_2[28];
  //   BA29 = in_2[29]; BA30 = in_2[30]; BA31 = in_2[31]; addOut0 = out_3[0]; addOut1 = out_3[1]; addOut2 = out_3[2];
  //   addOut3 = out_3[3]; addOut4 = out_3[4]; addOut5 = out_3[5]; addOut6 = out_3[6]; addOut7 = out_3[7];
  //   addOut8 = out_3[8]; addOut9 = out_3[9]; addOut10 = out_3[10]; addOut11 = out_3[11]; addOut12 = out_3[12];
  //   addOut13 = out_3[13]; addOut14 = out_3[14]; addOut15 = out_3[15]; addOut16 = out_3[16]; addOut17 = out_3[17];
  //   addOut18 = out_3[18]; addOut19 = out_3[19]; addOut20 = out_3[20]; addOut21 = out_3[21]; addOut22 = out_3[22];
  //   addOut23 = out_3[23]; addOut24 = out_3[24]; addOut25 = out_3[25]; addOut26 = out_3[26]; addOut27 = out_3[27];
  //   addOut28 = out_3[28]; addOut29 = out_3[29]; addOut30 = out_3[30]; addOut31 = out_3[31]
endmodule

module adderCirc (
  input  in_1,
  input  in_2,
  input  in_3,
  output out_4,
  output out_5
);

  wire and_1_out, and_2_out, and_3_out, and_4_out, and_5_out, and_6_out, and_7_out, not_1_out, not_2_out,
       not_3_out;

  not not_1 (not_1_out, in_1);
  not not_2 (not_2_out, in_2);
  not not_3 (not_3_out, in_3);
  and and_1 (and_1_out, not_1_out, not_2_out, in_3);
  and and_2 (and_2_out, not_1_out, in_2, not_3_out);
  and and_3 (and_3_out, in_1, not_2_out, not_3_out);
  and and_4 (and_4_out, in_1, in_2, in_3);
  and and_5 (and_5_out, not_1_out, in_2, in_3);
  and and_6 (and_6_out, in_1, not_2_out, in_3);
  and and_7 (and_7_out, in_1, in_2, not_3_out);
  or or_1 (out_4, and_1_out, and_2_out, and_3_out, and_4_out);
  or or_2 (out_5, and_4_out, and_5_out, and_6_out, and_7_out);
endmodule
