// Logisim project control_logic.circ as structural Verilog: 1 circuit, main circuit control_logic
module control_logic (
  input  [31:0] inst,
  input  BrEq,
  input  BrLt,
  output PCSel,
  output RegWEn,
  output [2:0] ImmSel,
  output BrUn,
  output ASel,
  output BSel,
  output [3:0] ALUSel,
  output MemRW,
  output [1:0] WBSel
);

  wire and_2_out, and_3_out, and_4_out, and_5_out, and_6_out, and_7_out, B_type, f3_0, f3_1, f3_2, f3_3,
       f3_4, f3_5, f3_6, f3_7, I_subtype13, or_1_out, or_3_out, or_6_out, R_type, U_type, xnor_1_out;
  wire [1:0] multiplexer_3_out, multiplexer_4_out;
  wire [2:0] adder_1_out, adder_2_out, multiplexer_1_out, multiplexer_2_out;
  wire [3:0] multiplexer_7_out, multiplexer_8_out, multiplexer_9_out, multiplexer_10_out, multiplexer_11_out;

  or or_1 (or_1_out, f3_4, f3_6);
  Adder #(.width(3)) adder_1 (.a(inst[6:4]), .b(3'b001), .out(adder_1_out));  // open: cin, cout
  Adder #(.width(3)) adder_2 (.a(inst[6:4]), .b(3'b111), .out(adder_2_out));  // open: cin, cout
  or or_2 (RegWEn, inst[2], inst[4], ~inst[5]);  // OR_Gate
  and and_1 (MemRW, ~inst[4], inst[5], ~inst[6]);  // AND_Gate
  and and_2 (and_2_out, ~inst[4], ~inst[5], ~inst[6]);  // AND_Gate
  and and_3 (and_3_out, inst[2], inst[5], inst[6]);
  Multiplexer #(.width(3), .enable("false")) multiplexer_1 (
    .in0(inst[6:4]), .in1(adder_1_out), .out(multiplexer_1_out), .sel(inst[2]));
  Multiplexer #(.width(3), .enable("false")) multiplexer_2 (
    .in0(inst[6:4]), .in1(adder_2_out), .out(multiplexer_2_out), .sel(inst[3]));
  Multiplexer #(.width(2), .enable("false")) multiplexer_3 (
    .in0(2'b00), .in1(2'b01), .out(multiplexer_3_out), .sel(and_2_out));
  Multiplexer #(.width(2), .enable("false")) multiplexer_4 (
    .in0(2'b00), .in1(2'b10), .out(multiplexer_4_out), .sel(and_3_out));
  and and_4 (and_4_out, f3_1, ~BrEq);  // AND_Gate
  and and_5 (and_5_out, f3_0, BrEq);
  and and_6 (and_6_out, or_1_out, BrLt);
  Multiplexer #(.width(3), .enable("false")) multiplexer_5 (
    .in0(multiplexer_1_out), .in1(multiplexer_2_out), .out(ImmSel), .sel(inst[3]));
  Multiplexer #(.width(2), .enable("false")) multiplexer_6 (
    .in0(multiplexer_3_out), .in1(multiplexer_4_out), .out(WBSel), .sel(and_3_out));
  or or_3 (or_3_out, and_4_out, and_5_out, and_6_out);
  or or_4 (PCSel, and_3_out, and_7_out);
  and and_7 (and_7_out, B_type, or_3_out);
  Demultiplexer #(.select(3), .enable("false")) demultiplexer_1 (
    .out0(f3_0), .out1(f3_1), .out2(f3_2), .out3(f3_3), .out4(f3_4), .out5(f3_5), .out6(f3_6), .out7(f3_7),
    .in(1'b1), .sel(inst[14:12]));
  xnor xnor_1 (xnor_1_out, inst[2], inst[3]);
  or or_5 (BSel, inst[2], ~inst[4], ~inst[5]);  // OR_Gate
  not not_1 (R_type, BSel);
  and and_8 (B_type, ~inst[2], ~inst[3], inst[5], inst[6]);  // AND_Gate
  and and_9 (U_type, inst[2], ~inst[3], inst[4], inst[5]);  // AND_Gate
  and and_10 (I_subtype13, ~inst[2], ~inst[3], inst[4], ~inst[5], ~inst[6]);  // AND_Gate
  and and_11 (ASel, xnor_1_out, inst[5], inst[6]);
  and and_12 (BrUn, B_type, f3_6);
  Multiplexer #(.width(4), .enable("false")) multiplexer_7 (
    .in0(4'b1010), .in1(4'b0000), .out(multiplexer_7_out), .sel(I_subtype13));
  Multiplexer #(.width(4), .enable("false")) multiplexer_8 (
    .in0(4'b1100), .in1(4'b0000), .out(multiplexer_8_out), .sel(I_subtype13));
  Multiplexer #(.width(4), .enable("false")) multiplexer_9 (
    .in0(4'b1001), .in1(4'b0001), .out(multiplexer_9_out), .sel(I_subtype13));
  Multiplexer #(.select(5), .width(4), .enable("false")) multiplexer_10 (
    .in0(4'b0000), .in1(multiplexer_7_out), .in2(multiplexer_8_out), .in3(4'b0000), .in4(4'b0110),
    .in5(4'b1110), .in8(4'b0111), .in9(4'b0111), .in10(4'b0111), .in11(4'b0111), .in13(4'b1011),
    .in16(4'b0011), .in17(4'b0011), .in18(4'b0011), .in19(4'b0011), .in20(4'b0100), .in21(4'b1000),
    .in22(4'b0101), .in24(4'b0010), .in25(4'b0010), .in26(4'b0010), .in27(4'b0010), .in28(4'b0001),
    .in29(multiplexer_9_out), .in30(4'b0001), .in31(4'b0001), .out(multiplexer_10_out),
    .sel({inst[14:12], inst[30], inst[25]}));  // open: in6, in7, in12, in14, in15, in23
  Multiplexer #(.width(4), .enable("false")) multiplexer_11 (
    .in0(4'b0000), .in1(multiplexer_10_out), .out(multiplexer_11_out), .sel(or_6_out));
  or or_6 (or_6_out, R_type, I_subtype13);
  Multiplexer #(.width(4), .enable("false")) multiplexer_12 (
    .in0(multiplexer_11_out), .in1(4'b1101), .out(ALUSel), .sel(U_type));

  // Other names for the same wires on the sheet: func7[6:0] = inst[31:25]; func3[2:0] = inst[14:12];
  //   op[6:0] = inst[6:0]; rd[4:0] = inst[11:7]; r1[4:0] = inst[19:15]; r2[4:0] = inst[24:20]

  // Notes on the sheet:
  //   B-Type and S-Type
  //   S-Type
  //   I-Type: load cmd
  //   jal and jalr cmd
  //   INPUTS to your circuit
  //   DON'T CHANGE THE LOCATIONS OF THE INPUTS AND OUTPUTS!
  //   OUTPUT from your circuit
  //   B-Type and J-Type
  //   Non R-Type
endmodule
