// Logisim project cpu.circ as structural Verilog: 1 circuit, main circuit main
module main (
  input  [31:0] INSTRUCTION,
  input  CLOCK,
  output [31:0] PROGRAM_COUNTER,
  output [31:0] ra,
  output [31:0] sp,
  output [31:0] t0,
  output [31:0] t1,
  output [31:0] t2,
  output [31:0] s0,
  output [31:0] s1,
  output [31:0] a0
);

  wire ASel, BrEq, BrLt, BrUn, BSel, DMEM_p1, DMEM_p2, MemRW, PCSel, rwe;
  wire [1:0] WBSel;
  wire [2:0] immSel;
  wire [3:0] ALUSel;
  wire [4:0] reg2;
  wire [31:0] ALU_out, DMEM_out, immOut, INSTRUCTION1, multiplexer_1_out, multiplexer_2_out,
       multiplexer_3_out, PC, PC4, rs1_out, rs2_out, undriven, writeBack;

  control_logic control_logic_1 (
    .BSel(BSel), .BrUn(BrUn), .RegWEn(rwe), .ImmSel(immSel), .ASel(ASel), .PCSel(PCSel), .BrLt(BrLt),
    .BrEq(BrEq), .inst(INSTRUCTION1), .ALUSel(ALUSel), .MemRW(MemRW), .WBSel(WBSel));
  Multiplexer #(.width(32), .enable("false")) multiplexer_1 (
    .in0(INSTRUCTION), .in1(32'h13), .out(multiplexer_1_out), .sel(PCSel));
  imm_gen imm_gen_1 (.ImmSel(immSel), .imm(immOut), .inst(INSTRUCTION1));
  // inst1 inst1_1: pin names not known
  // pc pc_1: pin names not known
  alu alu_1 (.Result(PC4), .A(PC), .B(32'h4));  // open: ALUSel, in_5
  regfile_main RegFile (
    .rs2(reg2), .rd(INSTRUCTION1[11:7]), .Read_Data_1(rs1_out), .Read_Data_2(rs2_out), .ra(ra), .sp(sp),
    .t0(t0), .t1(t1), .t2(t2), .s0(s0), .s1(s1), .a0(a0), .rs1(INSTRUCTION1[19:15]), .Write_Data(writeBack),
    .RegWEn(rwe), .clk(CLOCK));
  Multiplexer #(.width(32), .enable("false")) multiplexer_2 (
    .in0(rs1_out), .in1(undriven), .out(multiplexer_2_out), .sel(ASel));
  Multiplexer #(.width(32), .enable("false")) multiplexer_3 (
    .in0(rs2_out), .in1(immOut), .out(multiplexer_3_out), .sel(BSel));
  alu Arithmetic_Logic_Unit (
    .ALUSel(ALUSel), .Result(ALU_out), .A(multiplexer_2_out), .B(multiplexer_3_out));  // open: in_5
  branch_comp branch_comp_1 (.BrEq(BrEq), .BrUn(BrUn), .rs1(rs1_out), .BrLt(BrLt), .rs2(rs2_out), .out_6(BrLt));
  // mem_main DMEM: pin names not known; wires that end beside it: DMEM_p1, DMEM_p2, CLOCK, MemRW, DMEM_out
  Multiplexer #(.select(2), .width(32), .enable("false")) multiplexer_4 (
    .in0(ALU_out), .in2(DMEM_out), .in3(PC4), .out(writeBack), .sel(WBSel));  // open: in1

  // Other names for the same wires on the sheet: clk = CLOCK; reg1[4:0] = INSTRUCTION1[19:15];
  //   regD[4:0] = INSTRUCTION1[11:7]

  // Notes on the sheet:
  //   Output
  //   IMEM (do **NOT** move this)
  //   Inputs
  //   It is OK to move the PC, RegFile, ALU, MEM, Branch Comp, Imm Gen, and Control Logic to wherever is most convenient for you when constructing your CPU, and to delete this text
  //   Inputs/Outputs for testing. Do **NOT** move these.
endmodule
