// Logisim project regfile.circ as structural Verilog: 4 circuits, main circuit main
module main (
  input  [4:0] rs1,
  input  [4:0] rs2,
  input  [4:0] rd,
  input  [31:0] Write_Data,
  input  RegWEn,
  input  clk,
  output [31:0] ra,
  output [31:0] sp,
  output [31:0] t0,
  output [31:0] t1,
  output [31:0] t2,
  output [31:0] s0,
  output [31:0] s1,
  output [31:0] a0,
  output [31:0] Read_Data_1,
  output [31:0] Read_Data_2
);

  wire decoder_1_out0, WE_X1, WE_X2, WE_X5, WE_X6, WE_X7, WE_X8, WE_X9, WE_X10;
  wire [31:0] x0;

  Decoder #(.select(5)) decoder_1 (
    .out0(decoder_1_out0), .out1(WE_X1), .out2(WE_X2), .out5(WE_X5), .out6(WE_X6), .out7(WE_X7),
    .out8(WE_X8), .out9(WE_X9), .out10(WE_X10), .sel(rd));  // open: out3, out4, out11, out12, out13, out14, out15, out16, out17, out18, out19, out20, out21, out22, out23, out24, out25, out26, out27, out28, out29, out30, out31, en
  register_basic register_basic_1 (.write_enable(1'b0), .clck(clk), .data_in({32{1'b0}}), .data_out(x0));
  register_basic register_basic_2 (.write_enable(WE_X2), .clck(clk), .data_in(Write_Data), .data_out(sp));
  register_basic register_basic_3 (.write_enable(WE_X1), .clck(clk), .data_in(Write_Data), .data_out(ra));
  read_register read_register_1 (
    .x0(x0), .x1(ra), .x2(sp), .x5(t0), .x6(t1), .x7(t2), .x8(s0), .x9(s1), .x10(a0), .rs(rs1),
    .register_output(Read_Data_1));
  register_basic register_basic_4 (.write_enable(WE_X5), .clck(clk), .data_in(Write_Data), .data_out(t0));
  register_basic register_basic_5 (.write_enable(WE_X6), .clck(clk), .data_in(Write_Data), .data_out(t1));
  register_basic register_basic_6 (.write_enable(WE_X7), .clck(clk), .data_in(Write_Data), .data_out(t2));
  read_register read_register_2 (
    .x0(x0), .x1(ra), .x2(sp), .x5(t0), .x6(t1), .x7(t2), .x8(s0), .x9(s1), .x10(a0), .rs(rs2),
    .register_output(Read_Data_2));
  register_basic register_basic_7 (.write_enable(WE_X10), .clck(clk), .data_in(Write_Data), .data_out(a0));
  register_basic register_basic_8 (.write_enable(WE_X8), .clck(clk), .data_in(Write_Data), .data_out(s0));
  register_basic register_basic_9 (.write_enable(WE_X9), .clck(clk), .data_in(Write_Data), .data_out(s1));

  // Other names for the same wires on the sheet: read_data1[31:0] = Read_Data_1; read_data2[31:0] = Read_Data_2;
  //   read_reg1[4:0] = rs1; read_reg2[4:0] = rs2; write_en = RegWEn; write_reg[4:0] = rd

  // Notes on the sheet:
  //   INPUTS to your circuit
  //   DON'T CHANGE THE LOCATIONS OF THE INPUTS AND OUTPUTS!
  //   These are DEBUG/TEST outputs from your circuit.
  //   OUTPUTS from your circuit
endmodule

module register_basic (
  input  write_enable,
  input  clck,
  input  [31:0] data_in,
  output [31:0] data_out
);

  wire and_1_out;

  and and_1 (and_1_out, write_enable, clck);
  D_Flip_Flop d_ff_1 (.D(data_in[0]), .clk(and_1_out), .Q(data_out[0]));  // open: Qn, preset, reset
  D_Flip_Flop d_ff_2 (.D(data_in[1]), .clk(and_1_out), .Q(data_out[1]));  // open: Qn, preset, reset
  D_Flip_Flop d_ff_3 (.D(data_in[2]), .clk(and_1_out), .Q(data_out[2]));  // open: Qn, preset, reset
  D_Flip_Flop d_ff_4 (.D(data_in[3]), .clk(and_1_out), .Q(data_out[3]));  // open: Qn, preset, reset
  D_Flip_Flop d_ff_5 (.D(data_in[4]), .clk(and_1_out), .Q(data_out[4]));  // open: Qn, preset, reset
  D_Flip_Flop d_ff_6 (.D(data_in[5]), .clk(and_1_out), .Q(data_out[5]));  // open: Qn, preset, reset
  D_Flip_Flop d_ff_7 (.D(data_in[6]), .clk(and_1_out), .Q(data_out[6]));  // open: Qn, preset, reset
  D_Flip_Flop d_ff_8 (.D(data_in[7]), .clk(and_1_out), .Q(data_out[7]));  // open: Qn, preset, reset
  D_Flip_Flop d_ff_9 (.D(data_in[8]), .clk(and_1_out), .Q(data_out[8]));  // open: Qn, preset, reset
  D_Flip_Flop d_ff_10 (.D(data_in[9]), .clk(and_1_out), .Q(data_out[9]));  // open: Qn, preset, reset
  D_Flip_Flop d_ff_11 (.D(data_in[10]), .clk(and_1_out), .Q(data_out[10]));  // open: Qn, preset, reset
  D_Flip_Flop d_ff_12 (.D(data_in[11]), .clk(and_1_out), .Q(data_out[11]));  // open: Qn, preset, reset
  D_Flip_Flop d_ff_13 (.D(data_in[12]), .clk(and_1_out), .Q(data_out[12]));  // open: Qn, preset, reset
  D_Flip_Flop d_ff_14 (.D(data_in[13]), .clk(and_1_out), .Q(data_out[13]));  // open: Qn, preset, reset
  D_Flip_Flop d_ff_15 (.D(data_in[14]), .clk(and_1_out), .Q(data_out[14]));  // open: Qn, preset, reset
  D_Flip_Flop d_ff_16 (.D(data_in[15]), .clk(and_1_out), .Q(data_out[15]));  // open: Qn, preset, reset
  D_Flip_Flop d_ff_17 (.D(data_in[16]), .clk(and_1_out), .Q(data_out[16]));  // open: Qn, preset, reset
  D_Flip_Flop d_ff_18 (.D(data_in[17]), .clk(and_1_out), .Q(data_out[17]));  // open: Qn, preset, reset
  D_Flip_Flop d_ff_19 (.D(data_in[18]), .clk(and_1_out), .Q(data_out[18]));  // open: Qn, preset, reset
  D_Flip_Flop d_ff_20 (.D(data_in[19]), .clk(and_1_out), .Q(data_out[19]));  // open: Qn, preset, reset
  D_Flip_Flop d_ff_21 (.D(data_in[20]), .clk(and_1_out), .Q(data_out[20]));  // open: Qn, preset, reset
  D_Flip_Flop d_ff_22 (.D(data_in[21]), .clk(and_1_out), .Q(data_out[21]));  // open: Qn, preset, reset
  D_Flip_Flop d_ff_23 (.D(data_in[22]), .clk(and_1_out), .Q(data_out[22]));  // open: Qn, preset, reset
  D_Flip_Flop d_ff_24 (.D(data_in[23]), .clk(and_1_out), .Q(data_out[23]));  // open: Qn, preset, reset
  D_Flip_Flop d_ff_25 (.D(data_in[24]), .clk(and_1_out), .Q(data_out[24]));  // open: Qn, preset, reset
  D_Flip_Flop d_ff_26 (.D(data_in[25]), .clk(and_1_out), .Q(data_out[25]));  // open: Qn, preset, reset
  D_Flip_Flop d_ff_27 (.D(data_in[26]), .clk(and_1_out), .Q(data_out[26]));  // open: Qn, preset, reset
  D_Flip_Flop d_ff_28 (.D(data_in[27]), .clk(and_1_out), .Q(data_out[27]));  // open: Qn, preset, reset
  D_Flip_Flop d_ff_29 (.D(data_in[28]), .clk(and_1_out), .Q(data_out[28]));  // open: Qn, preset, reset
  D_Flip_Flop d_ff_30 (.D(data_in[29]), .clk(and_1_out), .Q(data_out[29]));  // open: Qn, preset, reset
  D_Flip_Flop d_ff_31 (.D(data_in[30]), .clk(and_1_out), .Q(data_out[30]));  // open: Qn, preset, reset
  D_Flip_Flop d_ff_32 (.D(data_in[31]), .clk(and_1_out), .Q(data_out[31]));  // open: Qn, preset, reset

  // Other names for the same wires on the sheet: D1 = data_in[0]; D2 = data_in[1]; D3 = data_in[2]; D4 = data_in[3];
  //   D5 = data_in[4]; D6 = data_in[5]; D7 = data_in[6]; D8 = data_in[7]; D9 = data_in[8]; D10 = data_in[9];
  //   D11 = data_in[10]; D12 = data_in[11]; D13 = data_in[12]; D14 = data_in[13]; D15 = data_in[14];
  //   D16 = data_in[15]; D17 = data_in[16]; D18 = data_in[17]; D19 = data_in[18]; D20 = data_in[19];
  //   D21 = data_in[20]; D22 = data_in[21]; D23 = data_in[22]; D24 = data_in[23]; D25 = data_in[24];
  //   D26 = data_in[25]; D27 = data_in[26]; D28 = data_in[27]; D29 = data_in[28]; D30 = data_in[29];
  //   D31 = data_in[30]; D32 = data_in[31]; S1 = data_out[0]; S2 = data_out[1]; S3 = data_out[2]; S4 = data_out[3];
  //   S5 = data_out[4]; S6 = data_out[5]; S7 = data_out[6]; S8 = data_out[7]; S9 = data_out[8]; S10 = data_out[9];
  //   S11 = data_out[10]; S12 = data_out[11]; S13 = data_out[12]; S14 = data_out[13]; S15 = data_out[14];
  //   S16 = data_out[15]; S17 = data_out[16]; S18 = data_out[17]; S19 = data_out[18]; S20 = data_out[19];
  //   S21 = data_out[20]; S22 = data_out[21]; S23 = data_out[22]; S24 = data_out[23]; S25 = data_out[24];
  //   S26 = data_out[25]; S27 = data_out[26]; S28 = data_out[27]; S29 = data_out[28]; S30 = data_out[29];
  //   S31 = data_out[30]; S32 = data_out[31]
endmodule

module read_register (
  input  [31:0] x0,
  input  [31:0] x1,
  input  [31:0] x2,
  input  [31:0] x5,
  input  [31:0] x6,
  input  [31:0] x7,
  input  [31:0] x8,
  input  [31:0] x9,
  input  [31:0] x10,
  input  [4:0] rs,
  output [31:0] register_output
);

  Multiplexer #(.select(5), .width(32), .enable("false")) multiplexer_1 (
    .in0(x0), .in1(x1), .in2(x2), .in3({32{1'b0}}), .in4({32{1'b0}}), .in5(x5), .in6(x6), .in7(x7), .in8(x8),
    .in9(x9), .in10(x10), .in11({32{1'b0}}), .in12({32{1'b0}}), .in13({32{1'b0}}), .in14({32{1'b0}}),
    .in15({32{1'b0}}), .in16({32{1'b0}}), .in17({32{1'b0}}), .in18({32{1'b0}}), .in19({32{1'b0}}),
    .in20({32{1'b0}}), .in21({32{1'b0}}), .in22({32{1'b0}}), .in23({32{1'b0}}), .in24({32{1'b0}}),
    .in25({32{1'b0}}), .in26({32{1'b0}}), .in27({32{1'b0}}), .in28({32{1'b0}}), .in29({32{1'b0}}),
    .in30({32{1'b0}}), .in31({32{1'b0}}), .out(register_output), .sel(rs));
endmodule

module inst1 (
);

  wire clk;
  wire [31:0] INSTRUCTION, INSTRUCTION1;

  Register #(.width(32), .trigger("falling")) register_1 (
    .D(INSTRUCTION), .clk(clk), .Q(INSTRUCTION1));  // open: en, clr
endmodule
